# Fritzing sketch Project build (saved by Fritzing 0.9.3b)
breadboards: 1

parts:
  Part1 = Arduino Uno (Rev3) - ICSP
  LED2 = smd LED [color="Red (633nm)" package="0603 [SMD]"]
  LED3 = smd LED [color="Green (555nm)" package="0603 [SMD]"]
  LED4 = smd LED [color="Green (555nm)" package="0603 [SMD]"]
  LED5 = smd LED [color="Red (633nm)" package="0603 [SMD]"]
  R1 = Resistor [tolerance=±5% resistance=220 package="0603 [SMD]"]
  R2 = Resistor [tolerance=±5% resistance=220 package="0603 [SMD]"]
  R3 = Resistor [tolerance=±5% resistance=220 package="0603 [SMD]"]
  R4 = Resistor [tolerance=±5% resistance=220 package="0603 [SMD]"]
  R5 = PHOTOCELL [package=photocell-kit]
  R6 = Resistor [tolerance=±5% resistance=220 package="0805 [SMD]"]

nets:
  N1: Part1.A0, R5.P$2, R6.Pin_0
  N2: Part1.ICSP_MISO, Part1.D12/MISO, R2.Pin_1
  N3: Part1.ICSP_MOSI, Part1.D11_PWM/MOSI, R3.Pin_1
  N4: Part1.D10_PWM/SS, R4.Pin_1
  N5: Part1.D13/SCK, R1.Pin_1
  N6: Part1.GND, LED2.cathode, LED3.cathode, LED5.cathode, R6.Pin_1
  N7: LED2.anode, R2.Pin_0
  N8: LED3.anode, R3.Pin_0
  N9: LED4.anode, R1.Pin_0
  N10: LED5.anode, R4.Pin_0
